# Fritzing sketch DDR (saved by Fritzing 0.9.2b)
breadboards: 1

parts:
  パーツ1 = Arduino Uno (Rev3)
  Disp1 = LBT2088AH [part_number=1588BS]
  R1 = Resistor [tolerance=±5% resistance=220 package=THT]
  R2 = Resistor [tolerance=±5% resistance=220 package=THT]
  R3 = Resistor [tolerance=±5% resistance=220 package=THT]
  R4 = Resistor [tolerance=±5% resistance=220 package=THT]
  R5 = Resistor [tolerance=±5% resistance=220 package=THT]
  R6 = Resistor [tolerance=±5% resistance=220 package=THT]
  R7 = Resistor [tolerance=±5% resistance=220 package=THT]
  R8 = Resistor [tolerance=±5% resistance=220 package=THT]
  パーツ2 = Thumb Joystick

nets:
  N1: パーツ1.A0, Disp1.pin_4
  N2: パーツ1.A1, Disp1.pin_3
  N3: パーツ1.A2, R3.Pin_1
  N4: パーツ1.A3, R1.Pin_1
  N5: パーツ1.A4/SDA, パーツ2.HORZ
  N6: パーツ1.A5/SCL, パーツ2.VERT
  N7: パーツ1.D8, Disp1.pin_11
  N8: パーツ1.D9_PWM, R7.Pin_1
  N9: パーツ1.D10_PWM/SS, Disp1.pin_13
  N10: パーツ1.D11_PWM/MOSI, R8.Pin_1
  N11: パーツ1.D12/MISO, Disp1.pin_15
  N12: パーツ1.D13/SCK, Disp1.pin_16
  N13: パーツ1.D2, R2.Pin_1
  N14: パーツ1.D3_PWM, Disp1.pin_6
  N15: パーツ1.D4, R4.Pin_1
  N16: パーツ1.D5_PWM, R5.Pin_1
  N17: パーツ1.D6_PWM, R6.Pin_1
  N18: パーツ1.D7, Disp1.pin_10
  5V: パーツ1.5V, パーツ2.VCC
  GND: パーツ1.GND, パーツ2.GND
  N19: Disp1.pin1, R1.Pin_0
  N20: Disp1.pin2, R3.Pin_0
  N21: Disp1.pin_5, R2.Pin_0
  N22: Disp1.pin_7, R4.Pin_0
  N23: Disp1.pin_8, R5.Pin_0
  N24: Disp1.pin_9, R6.Pin_0
  N25: Disp1.pin_12, R7.Pin_0
  N26: Disp1.pin_14, R8.Pin_0

notes:
  JoyStick
  Note: Vertical vs. Horizon
  16 15 14 13 12 11 10 9
  1588BS
  LED Matrix
  1 2 3 4 5 6 7 8
